// Logisim project alu.circ as structural Verilog: 2 circuits, main circuit alu
module alu (
  input  [31:0] ALU_A,
  input  [31:0] ALU_B,
  input  [3:0] ALU_op,
  output [2:0] CC,
  output [31:0] valE
);

  wire and_2_out, msb_1_msb, msb_2_msb, msb_3_msb, not_2_out, xnor_1_out, xor_2_out;
  wire [31:0] adder_1_out, and_1_out, multiplexer_1_out, not_1_out, shifter_1_out, xor_1_out;

  assign not_1_out = ~ALU_A;  // NOT_Gate not_1, 32 bits wide
  assign and_1_out = ALU_A & ALU_B;  // AND_Gate and_1, 32 bits wide
  assign xor_1_out = ALU_A ^ ALU_B;  // XOR_Gate xor_1, 32 bits wide
  Shifter #(.width(32), .shift("ar")) shifter_1 (.in(ALU_A), .\dist (5'b00001), .out(shifter_1_out));
  not not_2 (not_2_out, ALU_op[3]);
  MSB msb_1 (.MSB(msb_1_msb), .Value(ALU_B));
  MSB msb_2 (.MSB(msb_2_msb), .Value(multiplexer_1_out));
  Multiplexer #(.width(32), .enable("false")) multiplexer_1 (
    .in0(ALU_A), .in1(not_1_out), .out(multiplexer_1_out), .sel(ALU_op[0]));
  xnor xnor_1 (xnor_1_out, msb_2_msb, msb_1_msb);
  xor xor_2 (xor_2_out, msb_2_msb, msb_3_msb);
  MSB msb_3 (.MSB(msb_3_msb), .Value(adder_1_out));
  Adder #(.width(32)) adder_1 (.a(multiplexer_1_out), .b(ALU_B), .out(adder_1_out), .cin(ALU_op[0]));  // open: cout
  Multiplexer #(.disabled(0), .enable("false")) multiplexer_2 (
    .in0(and_2_out), .in1(1'b0), .out(CC[0]), .sel(ALU_op[1]));
  and and_2 (and_2_out, xnor_1_out, xor_2_out);
  Comparator #(.width(32)) comparator_1 (.a({32{1'b0}}), .b(valE), .eq(CC[2]));  // open: gt, lt
  MSB msb_4 (.MSB(CC[1]), .Value(valE));
  Multiplexer #(.select(3), .width(32)) multiplexer_3 (
    .in0(adder_1_out), .in1(adder_1_out), .in2(and_1_out), .in3(xor_1_out), .in4(shifter_1_out), .out(valE),
    .sel(ALU_op[2:0]), .en(not_2_out));  // open: in5, in6, in7

  // Notes on the sheet:
  //   add
  //   sub
  //   32-bit and
  //   32-bit xor
  //   or if both inputs are positive and result is negatve
  //   if both inputs are negative and result is positve
  //   an overflow occurred
  //   if sub carry in = 1
  //   (Zero Bit, Signed Bit, Overflow Bit)
  //   add
  //   sub
  //   and
  //   xor
  //   shift right
  //   is legit op?
  //   op selector
endmodule

module MSB (
  input  [31:0] Value,
  output MSB
);


  assign MSB = Value[31];
endmodule
