// Logisim project cndCode.circ as structural Verilog: 1 circuit, main circuit CND
module CND (
  input  [2:0] ZSO,
  input  [3:0] ifun,
  output CND
);

  wire not_1_out, not_2_out, not_3_out, not_4_out, or_1_out, xor_1_out;

  or or_1 (or_1_out, ZSO[2], xor_1_out);
  xor xor_1 (xor_1_out, ZSO[1], ZSO[0]);
  not not_1 (not_1_out, ZSO[2]);
  not not_2 (not_2_out, xor_1_out);
  not not_3 (not_3_out, or_1_out);
  Multiplexer #(.select(3), .disabled(0)) multiplexer_1 (
    .in0(1'b1), .in1(or_1_out), .in2(xor_1_out), .in3(ZSO[2]), .in4(not_1_out), .in5(not_2_out),
    .in6(not_3_out), .in7(1'b0), .out(CND), .sel(ifun[2:0]), .en(not_4_out));
  not not_4 (not_4_out, ifun[3]);

  // Notes on the sheet:
  //   Sample CND, from SWS
  //   always
  //   le
  //   l
  //   e
  //   ne
  //   ge
  //   g
endmodule
