// Logisim project microsequencer.circ as structural Verilog: 2 circuits, main circuit main
module main (
  input  [5:0] currentstate,
  input  [1:0] select,
  input  [3:0] icode,
  input  [5:0] valN,
  input  DMemDone,
  input  IMemDone,
  output [5:0] out_7
);

  microsequencer microsequencer_1 (
    .currentstate(currentstate), .valN(valN), .DMemDone(DMemDone), .icode(icode), .IMemDone(IMemDone),
    .select(select), .NextState(out_7));
endmodule

module microsequencer (
  input  [5:0] currentstate,
  input  [5:0] valN,
  input  DMemDone,
  input  [3:0] icode,
  input  IMemDone,
  input  [1:0] select,
  output [5:0] NextState
);

  wire [5:0] multiplexer_1_out, multiplexer_2_out;

  Multiplexer #(.width(6), .enable("false")) multiplexer_1 (
    .in0(currentstate), .in1(valN), .out(multiplexer_1_out), .sel(DMemDone));
  Multiplexer #(.width(6), .enable("false")) multiplexer_2 (
    .in0(currentstate), .in1({2'b11, icode}), .out(multiplexer_2_out), .sel(IMemDone));
  Multiplexer #(.select(2), .width(6)) multiplexer_3 (
    .in0(currentstate), .in1(valN), .in2(multiplexer_1_out), .in3(multiplexer_2_out), .out(NextState),
    .sel(select));  // open: en
endmodule
