// Logisim project regWriterReader.circ as structural Verilog: 4 circuits, main circuit main
module hw3 (
  input  [31:0] valE,
  input  [31:0] valM,
  input  [2:0] dstE,
  input  reqE,
  input  [2:0] dstM,
  input  reqM,
  input  clock,
  input  [2:0] srcA,
  input  [2:0] srcB,
  input  clr,
  output [31:0] valA,
  output [31:0] valB
);

  wire regreader_1_clr, regreader_1_clr_2, regreader_1_clr_3, regreader_1_clr_4, regreader_1_clr_5,
       regreader_1_clr_6, regreader_1_clr_7, regreader_1_clr_8, regwriter_1_clk, regwriter_1_clk_2,
       regwriter_1_clk_3, regwriter_1_clk_4, regwriter_1_clk_5, regwriter_1_clk_6, regwriter_1_clk_7,
       regwriter_1_clk_8, regwriter_1_en, regwriter_1_en_2, regwriter_1_en_3, regwriter_1_en_4,
       regwriter_1_en_5, regwriter_1_en_6, regwriter_1_en_7, regwriter_1_en_8;
  wire [31:0] register_1_q, register_2_q, register_3_q, register_4_q, register_5_q, register_6_q,
       register_7_q, register_8_q, regwriter_1_d0, regwriter_1_d1, regwriter_1_d2, regwriter_1_d3,
       regwriter_1_d4, regwriter_1_d5, regwriter_1_d6, regwriter_1_d7;

  regwriter regwriter_1 (
    .dstE(dstE), .reqE(reqE), .dstM(dstM), .reqM(reqM), .valE(valE), .valM(valM), .clock(clock),
    .D0(regwriter_1_d0), .EN(regwriter_1_en), .CLK(regwriter_1_clk), .D1(regwriter_1_d1),
    .EN_2(regwriter_1_en_2), .CLK_2(regwriter_1_clk_2), .D2(regwriter_1_d2), .EN_3(regwriter_1_en_3),
    .CLK_3(regwriter_1_clk_3), .D3(regwriter_1_d3), .EN_4(regwriter_1_en_4), .CLK_4(regwriter_1_clk_4),
    .D4(regwriter_1_d4), .EN_5(regwriter_1_en_5), .CLK_5(regwriter_1_clk_5), .D5(regwriter_1_d5),
    .EN_6(regwriter_1_en_6), .CLK_6(regwriter_1_clk_6), .D6(regwriter_1_d6), .EN_7(regwriter_1_en_7),
    .CLK_7(regwriter_1_clk_7), .D7(regwriter_1_d7), .EN_8(regwriter_1_en_8), .CLK_8(regwriter_1_clk_8));
  Register #(.width(32)) register_1 (
    .D(regwriter_1_d0), .en(regwriter_1_en), .Q(register_1_q), .clk(regwriter_1_clk), .clr(regreader_1_clr));
  Register #(.width(32)) register_2 (
    .D(regwriter_1_d1), .en(regwriter_1_en_2), .Q(register_2_q), .clk(regwriter_1_clk_2),
    .clr(regreader_1_clr_2));
  Register #(.width(32)) register_3 (
    .D(regwriter_1_d2), .en(regwriter_1_en_3), .Q(register_3_q), .clk(regwriter_1_clk_3),
    .clr(regreader_1_clr_3));
  Register #(.width(32)) register_4 (
    .D(regwriter_1_d3), .en(regwriter_1_en_4), .Q(register_4_q), .clk(regwriter_1_clk_4),
    .clr(regreader_1_clr_4));
  Register #(.width(32)) register_5 (
    .D(regwriter_1_d4), .en(regwriter_1_en_5), .Q(register_5_q), .clk(regwriter_1_clk_5),
    .clr(regreader_1_clr_5));
  Register #(.width(32)) register_6 (
    .D(regwriter_1_d5), .en(regwriter_1_en_6), .Q(register_6_q), .clk(regwriter_1_clk_6),
    .clr(regreader_1_clr_6));
  Register #(.width(32)) register_7 (
    .D(regwriter_1_d6), .en(regwriter_1_en_7), .Q(register_7_q), .clk(regwriter_1_clk_7),
    .clr(regreader_1_clr_7));
  Register #(.width(32)) register_8 (
    .D(regwriter_1_d7), .en(regwriter_1_en_8), .Q(register_8_q), .clk(regwriter_1_clk_8),
    .clr(regreader_1_clr_8));
  regreader regreader_1 (
    .srcA(srcA), .srcB(srcB), .valA(valA), .valB(valB), .reset(clr), .CLR(regreader_1_clr), .Q(register_1_q),
    .CLR_2(regreader_1_clr_2), .Q_2(register_2_q), .CLR_3(regreader_1_clr_3), .Q_3(register_3_q),
    .CLR_4(regreader_1_clr_4), .Q_4(register_4_q), .CLR_5(regreader_1_clr_5), .Q_5(register_5_q),
    .CLR_6(regreader_1_clr_6), .Q_6(register_6_q), .CLR_7(regreader_1_clr_7), .Q_7(register_7_q),
    .CLR_8(regreader_1_clr_8), .Q_8(register_8_q));

  // Notes on the sheet:
  //   D0
  //   en0
  //   clk0
  //   D7
  //   en7
  //   clk7
  //   R0
  //   R1
  //   R2
  //   R3
  //   R4
  //   R5
  //   R6
  //   R7
  //   Q0
  //   clr0
  //   Q7
  //   clr7
endmodule

module regwriter (
  input  [2:0] dstE,
  input  reqE,
  input  [2:0] dstM,
  input  reqM,
  input  [31:0] valE,
  input  [31:0] valM,
  input  clock,
  output [31:0] D0,
  output EN,
  output CLK,
  output [31:0] D1,
  output EN_2,
  output CLK_2,
  output [31:0] D2,
  output EN_3,
  output CLK_3,
  output [31:0] D3,
  output EN_4,
  output CLK_4,
  output [31:0] D4,
  output EN_5,
  output CLK_5,
  output [31:0] D5,
  output EN_6,
  output CLK_6,
  output [31:0] D6,
  output EN_7,
  output CLK_7,
  output [31:0] D7,
  output EN_8,
  output CLK_8
);

  wire comparator_1_eq, decoder_1_out0, decoder_1_out1, decoder_1_out2, decoder_1_out3, decoder_1_out4,
       decoder_1_out5, decoder_1_out6, decoder_1_out7, decoder_2_out0, decoder_2_out1, decoder_2_out2,
       decoder_2_out3, decoder_2_out4, decoder_2_out5, decoder_2_out6, decoder_2_out7, not_1_out;
  wire [7:0] and_14_out, and_15_out;
  wire [31:0] controlled_buffer_3_out, controlled_buffer_5_out, controlled_buffer_9_out,
       controlled_buffer_12_out, controlled_buffer_14_out, controlled_buffer_18_out,
       controlled_buffer_20_out, controlled_buffer_24_out;

  Decoder #(.select(3)) decoder_1 (
    .out0(decoder_1_out0), .out1(decoder_1_out1), .out2(decoder_1_out2), .out3(decoder_1_out3),
    .out4(decoder_1_out4), .out5(decoder_1_out5), .out6(decoder_1_out6), .out7(decoder_1_out7), .sel(dstE));  // open: en
  Decoder #(.select(3)) decoder_2 (
    .out0(decoder_2_out0), .out1(decoder_2_out1), .out2(decoder_2_out2), .out3(decoder_2_out3),
    .out4(decoder_2_out4), .out5(decoder_2_out5), .out6(decoder_2_out6), .out7(decoder_2_out7), .sel(dstM));  // open: en
  and and_1 (and_14_out[6], decoder_1_out6, reqE);
  and and_2 (and_14_out[7], decoder_1_out7, reqE);
  and and_3 (and_15_out[7], decoder_2_out7, reqM);
  and and_4 (and_14_out[5], decoder_1_out5, reqE);
  and and_5 (and_15_out[6], decoder_2_out6, reqM);
  and and_6 (and_14_out[4], decoder_1_out4, reqE);
  and and_7 (and_15_out[4], decoder_2_out4, reqM);
  and and_8 (and_15_out[5], decoder_2_out5, reqM);
  and and_9 (and_14_out[2], decoder_1_out2, reqE);
  and and_10 (and_14_out[3], decoder_1_out3, reqE);
  and and_11 (and_15_out[3], decoder_2_out3, reqM);
  and and_12 (and_14_out[1], decoder_1_out1, reqE);
  and and_13 (and_15_out[2], decoder_2_out2, reqM);
  and and_14 (and_14_out[0], reqE, decoder_1_out0);
  and and_15 (and_15_out[0], reqM, decoder_2_out0);
  and and_16 (and_15_out[1], decoder_2_out1, reqM);
  Comparator #(.mode("unsigned")) comparator_1 (.a(and_14_out), .b(and_15_out), .eq(comparator_1_eq));  // open: gt, lt
  not not_1 (not_1_out, comparator_1_eq);
  assign D0 = and_14_out[0] ? valE : 32'bz;  // Controlled_Buffer controlled_buffer_1
  assign D0 = not_1_out ? controlled_buffer_3_out : 32'bz;  // Controlled_Buffer controlled_buffer_2
  assign controlled_buffer_3_out = and_15_out[0] ? valM : 32'bz;  // Controlled_Buffer controlled_buffer_3
  assign D1 = and_14_out[1] ? valE : 32'bz;  // Controlled_Buffer controlled_buffer_4
  assign controlled_buffer_5_out = and_15_out[1] ? valM : 32'bz;  // Controlled_Buffer controlled_buffer_5
  assign D1 = not_1_out ? controlled_buffer_5_out : 32'bz;  // Controlled_Buffer controlled_buffer_6
  assign D2 = and_14_out[2] ? valE : 32'bz;  // Controlled_Buffer controlled_buffer_7
  assign D2 = not_1_out ? controlled_buffer_9_out : 32'bz;  // Controlled_Buffer controlled_buffer_8
  assign controlled_buffer_9_out = and_15_out[2] ? valM : 32'bz;  // Controlled_Buffer controlled_buffer_9
  assign D3 = and_14_out[3] ? valE : 32'bz;  // Controlled_Buffer controlled_buffer_10
  assign D3 = not_1_out ? controlled_buffer_12_out : 32'bz;  // Controlled_Buffer controlled_buffer_11
  assign controlled_buffer_12_out = and_15_out[3] ? valM : 32'bz;  // Controlled_Buffer controlled_buffer_12
  assign D4 = and_14_out[4] ? valE : 32'bz;  // Controlled_Buffer controlled_buffer_13
  assign controlled_buffer_14_out = and_15_out[4] ? valM : 32'bz;  // Controlled_Buffer controlled_buffer_14
  assign D4 = not_1_out ? controlled_buffer_14_out : 32'bz;  // Controlled_Buffer controlled_buffer_15
  assign D5 = and_14_out[5] ? valE : 32'bz;  // Controlled_Buffer controlled_buffer_16
  assign D5 = not_1_out ? controlled_buffer_18_out : 32'bz;  // Controlled_Buffer controlled_buffer_17
  assign controlled_buffer_18_out = and_15_out[5] ? valM : 32'bz;  // Controlled_Buffer controlled_buffer_18
  assign D6 = and_14_out[6] ? valE : 32'bz;  // Controlled_Buffer controlled_buffer_19
  assign controlled_buffer_20_out = and_15_out[6] ? valM : 32'bz;  // Controlled_Buffer controlled_buffer_20
  assign D6 = not_1_out ? controlled_buffer_20_out : 32'bz;  // Controlled_Buffer controlled_buffer_21
  assign D7 = and_14_out[7] ? valE : 32'bz;  // Controlled_Buffer controlled_buffer_22
  assign D7 = not_1_out ? controlled_buffer_24_out : 32'bz;  // Controlled_Buffer controlled_buffer_23
  assign controlled_buffer_24_out = and_15_out[7] ? valM : 32'bz;  // Controlled_Buffer controlled_buffer_24
  or or_1 (EN, and_14_out[0], and_15_out[0]);
  or or_2 (EN_2, and_14_out[1], and_15_out[1]);
  or or_3 (EN_3, and_14_out[2], and_15_out[2]);
  or or_4 (EN_4, and_14_out[3], and_15_out[3]);
  or or_5 (EN_5, and_14_out[4], and_15_out[4]);
  or or_6 (EN_6, and_14_out[5], and_15_out[5]);
  or or_7 (EN_7, and_14_out[6], and_15_out[6]);
  or or_8 (EN_8, and_14_out[7], and_15_out[7]);

  assign CLK = clock;
  assign CLK_2 = clock;
  assign CLK_3 = clock;
  assign CLK_4 = clock;
  assign CLK_5 = clock;
  assign CLK_6 = clock;
  assign CLK_7 = clock;
  assign CLK_8 = clock;
endmodule

module regreader (
  input  [2:0] srcA,
  input  [2:0] srcB,
  input  [31:0] Q,
  input  [31:0] Q_2,
  input  [31:0] Q_3,
  input  reset,
  input  [31:0] Q_4,
  input  [31:0] Q_5,
  input  [31:0] Q_6,
  input  [31:0] Q_7,
  input  [31:0] Q_8,
  output CLR,
  output [31:0] valA,
  output [31:0] valB,
  output CLR_2,
  output CLR_3,
  output CLR_4,
  output CLR_5,
  output CLR_6,
  output CLR_7,
  output CLR_8
);

  wire [7:0] decoder_1_out7, decoder_2_out7;

  Decoder #(.select(3)) decoder_1 (
    .out0(decoder_1_out7[7]), .out1(decoder_1_out7[6]), .out2(decoder_1_out7[5]), .out3(decoder_1_out7[4]),
    .out4(decoder_1_out7[3]), .out5(decoder_1_out7[2]), .out6(decoder_1_out7[1]), .out7(decoder_1_out7[0]),
    .sel(srcA));  // open: en
  assign valA = decoder_1_out7[7] ? Q : 32'bz;  // Controlled_Buffer controlled_buffer_1
  assign valA = decoder_1_out7[6] ? Q_2 : 32'bz;  // Controlled_Buffer controlled_buffer_2
  assign valA = decoder_1_out7[5] ? Q_3 : 32'bz;  // Controlled_Buffer controlled_buffer_3
  assign valA = decoder_1_out7[4] ? Q_4 : 32'bz;  // Controlled_Buffer controlled_buffer_4
  assign valA = decoder_1_out7[3] ? Q_5 : 32'bz;  // Controlled_Buffer controlled_buffer_5
  assign valA = decoder_1_out7[2] ? Q_6 : 32'bz;  // Controlled_Buffer controlled_buffer_6
  assign valA = decoder_1_out7[1] ? Q_7 : 32'bz;  // Controlled_Buffer controlled_buffer_7
  assign valA = decoder_1_out7[0] ? Q_8 : 32'bz;  // Controlled_Buffer controlled_buffer_8
  Decoder #(.select(3)) decoder_2 (
    .out0(decoder_2_out7[7]), .out1(decoder_2_out7[6]), .out2(decoder_2_out7[5]), .out3(decoder_2_out7[4]),
    .out4(decoder_2_out7[3]), .out5(decoder_2_out7[2]), .out6(decoder_2_out7[1]), .out7(decoder_2_out7[0]),
    .sel(srcB));  // open: en
  assign valB = decoder_2_out7[7] ? Q : 32'bz;  // Controlled_Buffer controlled_buffer_9
  assign valB = decoder_2_out7[6] ? Q_2 : 32'bz;  // Controlled_Buffer controlled_buffer_10
  assign valB = decoder_2_out7[5] ? Q_3 : 32'bz;  // Controlled_Buffer controlled_buffer_11
  assign valB = decoder_2_out7[4] ? Q_4 : 32'bz;  // Controlled_Buffer controlled_buffer_12
  assign valB = decoder_2_out7[3] ? Q_5 : 32'bz;  // Controlled_Buffer controlled_buffer_13
  assign valB = decoder_2_out7[2] ? Q_6 : 32'bz;  // Controlled_Buffer controlled_buffer_14
  assign valB = decoder_2_out7[1] ? Q_7 : 32'bz;  // Controlled_Buffer controlled_buffer_15
  assign valB = decoder_2_out7[0] ? Q_8 : 32'bz;  // Controlled_Buffer controlled_buffer_16

  assign CLR = reset;
  assign CLR_2 = reset;
  assign CLR_3 = reset;
  assign CLR_4 = reset;
  assign CLR_5 = reset;
  assign CLR_6 = reset;
  assign CLR_7 = reset;
  assign CLR_8 = reset;

  // Notes on the sheet:
  //   for reg 0
  //   for reg 7
endmodule

module main (
  input  [31:0] in_1,
  input  [31:0] in_2,
  input  [2:0] in_3,
  input  in_4,
  input  [2:0] in_5,
  input  in_6,
  input  in_7,
  input  in_8,
  input  [2:0] in_9,
  input  [2:0] in_10
);

  hw3 hw3_1 (
    .valE(in_1), .valM(in_2), .dstE(in_3), .reqE(in_4), .dstM(in_5), .reqM(in_6), .clock(in_7), .srcA(in_9),
    .srcB(in_10), .clr(in_8));  // open: valA, valB
endmodule
