// Logisim project shims.circ as structural Verilog: 4 circuits, main circuit ishim
module ishim (
  input  req,
  input  [31:0] in_2,
  input  reset,
  input  clock,
  input  [7:0] in_5,
  output [7:0] out_6,
  output [7:0] out_7,
  output [7:0] out_8,
  output [7:0] out_9,
  output [7:0] out_10,
  output [7:0] out_11,
  output done,
  output RAMuse,
  output RAMread,
  output [31:0] when_not_done
);

  wire and_1_out, decoder_1_out0, decoder_1_out1, decoder_1_out2, decoder_1_out3, decoder_1_out4,
       decoder_1_out5, not_1_out, or_1_out;
  wire [2:0] _3bit_q;
  wire [31:0] n32_3bitadder_1_out_3;

  D_Flip_Flop d_ff_1 (.clk(clock), .D(req), .Q(RAMread), .Qn(done), .preset(1'b0), .en(done), .reset(or_1_out));
  Counter #(.width(3), .max('h7)) _3bit (
    .load(1'b0), .count(RAMread), .Q(_3bit_q), .clk(clock), .clr(or_1_out));  // open: D, carry
  or or_1 (or_1_out, and_1_out, reset);
  and and_1 (and_1_out, ~_3bit_q[0], _3bit_q[1], _3bit_q[2]);  // AND_Gate
  _32_3bitAdder u_32_3bitadder_1 (.in_1(in_2), .in_2(_3bit_q), .out_3(n32_3bitadder_1_out_3));
  not not_1 (not_1_out, done);
  assign when_not_done = not_1_out ? n32_3bitadder_1_out_3 : 32'bz;  // Controlled_Buffer controlled_buffer_1
  Decoder #(.select(3), .enable("false")) decoder_1 (
    .out0(decoder_1_out0), .out1(decoder_1_out1), .out2(decoder_1_out2), .out3(decoder_1_out3),
    .out4(decoder_1_out4), .out5(decoder_1_out5), .sel(_3bit_q));  // open: out6, out7
  Register register_1 (.D(in_5), .en(decoder_1_out0), .Q(out_6), .clk(clock), .clr(reset));
  Register register_2 (.D(in_5), .en(decoder_1_out1), .Q(out_7), .clk(clock), .clr(reset));
  Register register_3 (.D(in_5), .en(decoder_1_out2), .Q(out_8), .clk(clock), .clr(reset));
  Register register_4 (.D(in_5), .en(decoder_1_out3), .Q(out_9), .clk(clock), .clr(reset));
  Register register_5 (.D(in_5), .en(decoder_1_out4), .Q(out_10), .clk(clock), .clr(reset));
  Register register_6 (.D(in_5), .en(decoder_1_out5), .Q(out_11), .clk(clock), .clr(reset));

  assign RAMuse = RAMread;

  // Notes on the sheet:
  //   addr
  //   in use?
  //   state
  //   reach 5 then reset
  //   while not done
  //   RAMaddr not floating
  //   write to each register
  //   according to counter
  //   RAMaddr (32 bits)
  //   data from RAM (8 bits)
  //   byte 0
  //   byte 1
  //   byte 2
  //   byte 3
  //   byte 4
  //   byte 5
endmodule

module dshim (
  input  [31:0] in_1,
  input  [31:0] in_2,
  input  DMem_Write,
  input  req,
  input  reset,
  input  clock,
  input  [7:0] in_7,
  output [31:0] DataOut,
  output [7:0] out_9,
  output RAMwrite,
  output RAMread,
  output done,
  output RAMuse,
  output [31:0] then_be_floating
);

  wire and_3_out, d_ff_1_q, d_ff_1_qn, decoder_1_out0, decoder_1_out1, decoder_1_out2, decoder_1_out3,
       not_1_out, or_1_out;
  wire [2:0] _3bit_q;
  wire [7:0] multiplexer_1_out;
  wire [31:0] n32_3bitadder_1_out_3;

  D_Flip_Flop d_ff_1 (
    .clk(clock), .D(DMem_Write), .Q(d_ff_1_q), .Qn(d_ff_1_qn), .preset(1'b0), .en(done), .reset(reset));
  D_Flip_Flop in_use (.clk(clock), .D(req), .Q(RAMuse), .Qn(done), .preset(1'b0), .en(done), .reset(or_1_out));
  and and_1 (RAMwrite, RAMuse, d_ff_1_q);
  and and_2 (RAMread, d_ff_1_qn, RAMuse);
  Counter #(.width(3), .max('h7)) _3bit (
    .load(1'b0), .count(RAMuse), .Q(_3bit_q), .clk(clock), .clr(or_1_out));  // open: D, carry
  or or_1 (or_1_out, and_3_out, reset);
  and and_3 (and_3_out, ~_3bit_q[0], ~_3bit_q[1], _3bit_q[2]);  // AND_Gate
  _32_3bitAdder u_32_3bitadder_1 (.in_1(in_2), .in_2(_3bit_q), .out_3(n32_3bitadder_1_out_3));
  not not_1 (not_1_out, done);
  assign then_be_floating = not_1_out ? n32_3bitadder_1_out_3 : 32'bz;  // Controlled_Buffer controlled_buffer_1
  Decoder #(.select(3), .enable("false")) decoder_1 (
    .out0(decoder_1_out0), .out1(decoder_1_out1), .out2(decoder_1_out2), .out3(decoder_1_out3), .sel(_3bit_q));  // open: out4, out5, out6, out7
  Multiplexer #(.select(3), .width(8), .enable("false")) multiplexer_1 (
    .in0(in_1[7:0]), .in1(in_1[15:8]), .in2(in_1[23:16]), .in3(in_1[31:24]), .out(multiplexer_1_out),
    .sel(_3bit_q));  // open: in4, in5, in6, in7
  Register register_1 (.D(in_7), .en(decoder_1_out0), .Q(DataOut[7:0]), .clk(clock), .clr(reset));
  Register register_2 (.D(in_7), .en(decoder_1_out1), .Q(DataOut[15:8]), .clk(clock), .clr(reset));
  Register register_3 (.D(in_7), .en(decoder_1_out2), .Q(DataOut[23:16]), .clk(clock), .clr(reset));
  Register register_4 (.D(in_7), .en(decoder_1_out3), .Q(DataOut[31:24]), .clk(clock), .clr(reset));
  assign out_9 = RAMwrite ? multiplexer_1_out : 8'bz;  // Controlled_Buffer controlled_buffer_2

  // Notes on the sheet:
  //   data in
  //   address
  //   writing?
  //   reading?
  //   state
  //   reach 3 then reset
  //   adds a 32 and 3 bits
  //   RAMaddr (32 bits)
  //   if not currently
  //   writing/reading
  //   data from RAM (8 bits)
  //   data to RAM (8 bits)
endmodule

module shim_test (
  input  in_1,
  input  [31:0] in_2,
  input  in_3,
  input  in_4,
  input  in_5,
  input  in_6,
  input  in_7,
  input  [31:0] dataIn,
  input  [31:0] addr,
  input  in_10,
  input  in_11,
  input  in_12,
  output [7:0] out_13,
  output [7:0] out_14,
  output [7:0] out_15,
  output [7:0] out_16,
  output [7:0] out_17,
  output [7:0] out_18,
  output out_19,
  output [31:0] out_20,
  output out_21
);

  wire dshim_1_ramread, dshim_1_ramuse, dshim_1_ramwrite, ishim_1_p3, ishim_1_p6;
  wire [7:0] dshim_1_out_9, ishim_1_p7, ram_2_data;
  wire [9:0] bit_extender_1_out, bit_extender_2_out;
  wire [31:0] dshim_1_then_be_floating, ishim_1_p4;

  Bit_Extender #(.in_width(32), .out_width(10)) bit_extender_1 (.in(ishim_1_p4), .out(bit_extender_1_out));
  Bit_Extender #(.in_width(32), .out_width(10)) bit_extender_2 (
    .in(dshim_1_then_be_floating), .out(bit_extender_2_out));
  // ishim ishim_1: pin names not known; wires that end beside it: in_3, in_4, ishim_1_p3, ishim_1_p4, in_1, ishim_1_p6, ishim_1_p7, out_13, out_14, out_15, out_16, out_17, out_18, out_19
  RAM #(.addrWidth(10), .bus("separate")) ram_1 (
    .addr(bit_extender_1_out), .data(ishim_1_p7), .str(1'b0), .sel(ishim_1_p3), .clk(in_4), .ld(ishim_1_p6),
    .clr(in_5));  // open: din
  // Probe on ishim_1_p7
  dshim dshim_1 (
    .in_1(dataIn), .in_2(addr), .done(out_21), .req(in_6), .DMem_Write(in_7), .reset(in_10), .clock(in_11),
    .RAMuse(dshim_1_ramuse), .then_be_floating(dshim_1_then_be_floating), .out_9(dshim_1_out_9),
    .RAMread(dshim_1_ramread), .RAMwrite(dshim_1_ramwrite), .in_7(ram_2_data), .DataOut(out_20));
  // Probe on ram_2_data
  RAM #(.addrWidth(10), .bus("separate")) ram_2 (
    .addr(bit_extender_2_out), .din(dshim_1_out_9), .data(ram_2_data), .str(dshim_1_ramwrite),
    .sel(dshim_1_ramuse), .clk(in_11), .ld(dshim_1_ramread), .clr(in_12));
endmodule

module _32_3bitAdder (
  input  [31:0] in_1,
  input  [2:0] in_2,
  output [31:0] out_3
);

  wire [31:0] bit_extender_1_out;

  assign bit_extender_1_out = {{29{1'b0}}, in_2};  // Bit_Extender bit_extender_1
  Adder #(.width(32)) adder_1 (.a(in_1), .b(bit_extender_1_out), .out(out_3));  // open: cin, cout
endmodule
