// Logisim project Y86.circ as structural Verilog: 4 circuits, main circuit dpath
module dpath (
  input  Reset,
  output [3:0] ifun,
  output out_3,
  output [1:0] select
);

  wire aluBsel, aluOPsel, and_1_out, and_2_out, and_3_out, cnd_1_cnd, comparator_1_eq, comparator_2_gt,
       comparator_3_lt, comparator_4_gt, comparator_5_eq, comparator_6_eq, D_RAMread, D_RAMuse, D_RAMWrite,
       DMemReady, DMemReq, DMemWrite, dstEsel, dstMreq, I_RAMread, I_RAMuse, IMemReady, io_1_tty_clear,
       io_1_tty_clock, io_1_tty_enable, multiplexer_8_out, or_1_out, or_2_out, or_3_out, priv_bit,
       regreader_1_clr, regreader_1_clr_2, regreader_1_clr_3, regreader_1_clr_4, regreader_1_clr_5,
       regreader_1_clr_6, regreader_1_clr_7, regreader_1_clr_8, regwriter_1_clk, regwriter_1_clk_2,
       regwriter_1_clk_3, regwriter_1_clk_4, regwriter_1_clk_5, regwriter_1_clk_6, regwriter_1_clk_7,
       regwriter_1_clk_8, regwriter_1_en, regwriter_1_en_2, regwriter_1_en_3, regwriter_1_en_4,
       regwriter_1_en_5, regwriter_1_en_6, regwriter_1_en_7, regwriter_1_en_8;
  wire [1:0] aluAsel, dstEreq;
  wire [2:0] alu_1_cc, bit_extender_1_out, bit_extender_2_out, bit_extender_3_out, bit_extender_4_out, cc;
  wire [3:0] icode, isplit_1_ra, isplit_1_rb, multiplexer_5_out, multiplexer_6_out, multiplexer_7_out,
       multiplexer_11_out;
  wire [5:0] current_state_q, microsequencer_1_nextstate;
  wire [6:0] io_1_out_14;
  wire [7:0] D_Data_from_RAM, D_Data_to_RAM, I_Data_from_RAM, ishim_1_out_6, ishim_1_out_7, ishim_1_out_8,
       ishim_1_out_9, ishim_1_out_10, ishim_1_out_11;
  wire [7:2] rom_1_data;
  wire [23:0] bit_extender_5_out, bit_extender_6_out, FSMOut;
  wire [31:0] adder_1_out, alu_1_vale, D_RAMAddr, dshim_1_dataout, eax_q, ebp_q, ebx_q, ecx_q, edi_q, edx_q,
       esi_q, esp_q, I_RAMAddr, isplit_1_d_v, isplit_1_dest, MAR_q, MDR_q, multiplexer_1_out,
       multiplexer_2_out, multiplexer_3_out, multiplexer_4_out, multiplexer_9_out, multiplexer_10_out,
       multiplexer_12_out, multiplexer_13_out, PC_q, regreader_1_vala, regreader_1_valb, regwriter_1_d0,
       regwriter_1_d1, regwriter_1_d2, regwriter_1_d3, regwriter_1_d4, regwriter_1_d5, regwriter_1_d6,
       regwriter_1_d7;

  Clock #(.highDuration(16), .lowDuration(16)) Clock ();  // open: out
  Button button_1 (.out(out_3));
  Register #(.width(32)) PC (.D(multiplexer_2_out), .en(FSMOut[0]), .Q(PC_q), .clk(out_3), .clr(Reset));
  // Probe on FSMOut[22:21]
  // Probe on FSMOut[23]
  Register #(.width(6)) current_state (
    .D(microsequencer_1_nextstate), .Q(current_state_q), .clk(out_3), .clr(Reset));  // open: en
  // Probe on multiplexer_1_out
  Multiplexer #(.select(2), .width(32), .enable("false")) multiplexer_1 (
    .in0(32'h1), .in1(32'h2), .in2(32'h5), .in3(32'h6), .out(multiplexer_1_out), .sel(FSMOut[22:21]));
  // Probe on FSMOut[20]
  Adder #(.width(32)) adder_1 (.a(multiplexer_1_out), .b(PC_q), .out(adder_1_out));  // open: cin, cout
  // Probe on multiplexer_4_out
  CND cnd_1 (.ZSO(cc), .ifun(ifun), .CND(cnd_1_cnd));
  ishim ishim_1 (
    .in_2(PC_q), .req(FSMOut[23]), .reset(Reset), .clock(out_3), .RAMuse(I_RAMuse),
    .when_not_done(I_RAMAddr), .RAMread(I_RAMread), .in_5(I_Data_from_RAM), .done(IMemReady),
    .out_11(ishim_1_out_11), .out_6(ishim_1_out_6), .out_7(ishim_1_out_7), .out_8(ishim_1_out_8),
    .out_9(ishim_1_out_9), .out_10(ishim_1_out_10));
  // Probe on FSMOut[19]
  Multiplexer #(.select(2), .width(32), .enable("false")) multiplexer_2 (
    .in0(adder_1_out), .in1(multiplexer_4_out), .in2(dshim_1_dataout), .in3(multiplexer_3_out),
    .out(multiplexer_2_out), .sel(FSMOut[2:1]));
  Multiplexer #(.width(32), .enable("false")) multiplexer_3 (
    .in0(adder_1_out), .in1(multiplexer_4_out), .out(multiplexer_3_out), .sel(cnd_1_cnd));
  isplit isplit_1 (
    .B0(ishim_1_out_6), .B1(ishim_1_out_7), .B2(ishim_1_out_8), .B3(ishim_1_out_9), .B4(ishim_1_out_10),
    .B5(ishim_1_out_11), .icode(icode), .ifun(ifun), .rA(isplit_1_ra), .rB(isplit_1_rb),
    .Dest(isplit_1_dest), .D_V(isplit_1_d_v));
  // Probe on FSMOut[18]
  // Probe on dstEsel
  ROM #(.addrWidth(6), .dataWidth(32)) rom_1 (
    .addr(current_state_q),
    .data({FSMOut[23:18], dstEsel, dstEreq, dstMreq, aluAsel, aluBsel, aluOPsel, FSMOut[9:5], DMemReq, DMemWrite, FSMOut[2:0], rom_1_data, select}));  // open: sel
  // Probe on icode
  // Probe on ifun
  Multiplexer #(.width(32), .enable("false")) multiplexer_4 (
    .in0(isplit_1_dest), .in1(isplit_1_d_v), .out(multiplexer_4_out), .sel(FSMOut[20]));
  // Probe on dstEreq
  // Probe on isplit_1_ra
  // Probe on isplit_1_rb
  // Probe on dstMreq
  Multiplexer #(.width(4), .enable("false")) multiplexer_5 (
    .in0(isplit_1_rb), .in1(4'b0100), .out(multiplexer_5_out), .sel(dstEsel));
  Multiplexer #(.width(4), .enable("false")) multiplexer_6 (
    .in0(isplit_1_ra), .in1(4'b0100), .out(multiplexer_6_out), .sel(FSMOut[19]));
  Multiplexer #(.width(4), .enable("false")) multiplexer_7 (
    .in0(isplit_1_rb), .in1(4'b0100), .out(multiplexer_7_out), .sel(FSMOut[18]));
  // Probe on aluAsel
  Bit_Extender #(.in_width(4), .out_width(3)) bit_extender_1 (.in(multiplexer_5_out), .out(bit_extender_1_out));
  Multiplexer #(.select(2), .enable("false")) multiplexer_8 (
    .in0(1'b0), .in1(1'b1), .in2(cnd_1_cnd), .out(multiplexer_8_out), .sel(dstEreq));  // open: in3
  Bit_Extender #(.in_width(4), .out_width(3)) bit_extender_2 (.in(isplit_1_ra), .out(bit_extender_2_out));
  Bit_Extender #(.in_width(4), .out_width(3)) bit_extender_3 (.in(multiplexer_6_out), .out(bit_extender_3_out));
  Bit_Extender #(.in_width(4), .out_width(3)) bit_extender_4 (.in(multiplexer_7_out), .out(bit_extender_4_out));
  Comparator #(.width(4)) comparator_1 (.a(multiplexer_7_out), .b(4'b1111), .eq(comparator_1_eq));  // open: gt, lt
  // Probe on aluBsel
  regwriter regwriter_1 (
    .dstE(bit_extender_1_out), .reqE(multiplexer_8_out), .dstM(bit_extender_2_out), .reqM(dstMreq),
    .valE(alu_1_vale), .valM(dshim_1_dataout), .clock(out_3), .D0(regwriter_1_d0), .EN(regwriter_1_en),
    .CLK(regwriter_1_clk), .D1(regwriter_1_d1), .EN_2(regwriter_1_en_2), .CLK_2(regwriter_1_clk_2),
    .D2(regwriter_1_d2), .EN_3(regwriter_1_en_3), .CLK_3(regwriter_1_clk_3), .D3(regwriter_1_d3),
    .EN_4(regwriter_1_en_4), .CLK_4(regwriter_1_clk_4), .D4(regwriter_1_d4), .EN_5(regwriter_1_en_5),
    .CLK_5(regwriter_1_clk_5), .D5(regwriter_1_d5), .EN_6(regwriter_1_en_6), .CLK_6(regwriter_1_clk_6),
    .D6(regwriter_1_d6), .EN_7(regwriter_1_en_7), .CLK_7(regwriter_1_clk_7), .D7(regwriter_1_d7),
    .EN_8(regwriter_1_en_8), .CLK_8(regwriter_1_clk_8));
  Register #(.width(32)) eax (
    .D(regwriter_1_d0), .en(regwriter_1_en), .Q(eax_q), .clk(regwriter_1_clk), .clr(regreader_1_clr));
  Register #(.width(32)) ecx (
    .D(regwriter_1_d1), .en(regwriter_1_en_2), .Q(ecx_q), .clk(regwriter_1_clk_2), .clr(regreader_1_clr_2));
  Register #(.width(32)) edx (
    .D(regwriter_1_d2), .en(regwriter_1_en_3), .Q(edx_q), .clk(regwriter_1_clk_3), .clr(regreader_1_clr_3));
  Register #(.width(32)) ebx (
    .D(regwriter_1_d3), .en(regwriter_1_en_4), .Q(ebx_q), .clk(regwriter_1_clk_4), .clr(regreader_1_clr_4));
  Register #(.width(32)) esp (
    .D(regwriter_1_d4), .en(regwriter_1_en_5), .Q(esp_q), .clk(regwriter_1_clk_5), .clr(regreader_1_clr_5));
  Register #(.width(32)) ebp (
    .D(regwriter_1_d5), .en(regwriter_1_en_6), .Q(ebp_q), .clk(regwriter_1_clk_6), .clr(regreader_1_clr_6));
  Register #(.width(32)) esi (
    .D(regwriter_1_d6), .en(regwriter_1_en_7), .Q(esi_q), .clk(regwriter_1_clk_7), .clr(regreader_1_clr_7));
  Register #(.width(32)) edi (
    .D(regwriter_1_d7), .en(regwriter_1_en_8), .Q(edi_q), .clk(regwriter_1_clk_8), .clr(regreader_1_clr_8));
  // Probe on aluOPsel
  // Probe on FSMOut[9]
  regreader regreader_1 (
    .srcA(bit_extender_3_out), .srcB(bit_extender_4_out), .valA(regreader_1_vala), .valB(regreader_1_valb),
    .reset(Reset), .CLR(regreader_1_clr), .Q(eax_q), .CLR_2(regreader_1_clr_2), .Q_2(ecx_q),
    .CLR_3(regreader_1_clr_3), .Q_3(edx_q), .CLR_4(regreader_1_clr_4), .Q_4(ebx_q),
    .CLR_5(regreader_1_clr_5), .Q_5(esp_q), .CLR_6(regreader_1_clr_6), .Q_6(ebp_q),
    .CLR_7(regreader_1_clr_7), .Q_7(esi_q), .CLR_8(regreader_1_clr_8), .Q_8(edi_q));
  microsequencer microsequencer_1 (
    .currentstate(current_state_q), .valN(rom_1_data), .DMemDone(DMemReady), .icode(icode),
    .IMemDone(IMemReady), .select(select), .NextState(microsequencer_1_nextstate));
  // Probe on regreader_1_vala
  // Probe on regreader_1_valb
  // Probe on multiplexer_4_out
  // Probe on FSMOut[7]
  // Probe on FSMOut[8]
  Multiplexer #(.select(2), .width(32), .enable("false")) multiplexer_9 (
    .in0(regreader_1_vala), .in1(multiplexer_4_out), .in2(32'h4), .in3(32'hfffffffc),
    .out(multiplexer_9_out), .sel(aluAsel));
  or or_1 (or_1_out, aluBsel, comparator_1_eq);
  // Probe on FSMOut[6]
  Multiplexer #(.width(32), .enable("false")) multiplexer_10 (
    .in0(regreader_1_valb), .in1({32{1'b0}}), .out(multiplexer_10_out), .sel(or_1_out));
  alu alu_1 (
    .CC(alu_1_cc), .ALU_A(multiplexer_9_out), .valE(alu_1_vale), .ALU_B(multiplexer_10_out),
    .ALU_op(multiplexer_11_out));
  Multiplexer #(.width(4), .enable("false")) multiplexer_11 (
    .in0(4'b0000), .in1(ifun), .out(multiplexer_11_out), .sel(aluOPsel));
  // Probe on FSMOut[5]
  // Probe on DMemReq
  // Probe on cc
  Register #(.width(3)) u_CC (.D(alu_1_cc), .en(FSMOut[9]), .Q(cc), .clk(out_3), .clr(Reset));
  // Probe on DMemWrite
  // Probe on adder_1_out
  // Probe on alu_1_vale
  Multiplexer #(.width(32), .enable("false")) multiplexer_12 (
    .in0(regreader_1_vala), .in1(adder_1_out), .out(multiplexer_12_out), .sel(FSMOut[6]));
  Multiplexer #(.width(32), .enable("false")) multiplexer_13 (
    .in0(alu_1_vale), .in1(regreader_1_vala), .out(multiplexer_13_out), .sel(FSMOut[8]));
  // Probe on FSMOut[2:1]
  Register #(.width(32)) MDR (.D(multiplexer_12_out), .en(FSMOut[5]), .Q(MDR_q), .clk(out_3), .clr(Reset));
  Register #(.width(32)) MAR (.D(multiplexer_13_out), .en(FSMOut[7]), .Q(MAR_q), .clk(out_3), .clr(Reset));
  // Probe on FSMOut[0]
  // Probe on dshim_1_dataout
  Comparator #(.width(32), .mode("unsigned")) comparator_2 (
    .a(D_RAMAddr), .b(32'h3ff), .gt(comparator_2_gt));  // open: eq, lt
  Comparator #(.width(32), .mode("unsigned")) comparator_3 (
    .a(D_RAMAddr), .b(32'h10000), .lt(comparator_3_lt));  // open: gt, eq
  dshim dshim_1 (
    .in_1(MDR_q), .in_2(MAR_q), .done(DMemReady), .req(DMemReq), .DMem_Write(DMemWrite), .reset(Reset),
    .clock(out_3), .RAMuse(D_RAMuse), .then_be_floating(D_RAMAddr), .out_9(D_Data_to_RAM),
    .RAMread(D_RAMread), .RAMwrite(D_RAMWrite), .in_7(D_Data_from_RAM), .DataOut(dshim_1_dataout));
  and and_1 (and_1_out, comparator_2_gt, comparator_3_lt, D_RAMuse);
  Comparator #(.width(32), .mode("unsigned")) comparator_4 (
    .a(32'h400), .b(I_RAMAddr), .gt(comparator_4_gt));  // open: eq, lt
  Bit_Extender #(.in_width(32), .out_width(24)) bit_extender_5 (.in(D_RAMAddr), .out(bit_extender_5_out));
  Bit_Extender #(.in_width(32), .out_width(24)) bit_extender_6 (.in(I_RAMAddr), .out(bit_extender_6_out));
  and and_2 (and_2_out, comparator_4_gt, I_RAMuse, I_RAMread);
  ROM #(.addrWidth(24)) rom_2 (.addr(bit_extender_6_out), .data(I_Data_from_RAM), .sel(and_2_out));
  and and_3 (and_3_out, ~priv_bit, D_RAMuse);  // AND_Gate
  RAM #(.addrWidth(24), .bus("separate")) ram_1 (
    .addr(bit_extender_5_out), .din(D_Data_to_RAM), .data(D_Data_from_RAM), .str(D_RAMWrite),
    .sel(and_1_out), .clk(out_3), .ld(D_RAMread), .clr(Reset));
  io io_1 (
    .RAM_Use(and_3_out), .in_4(D_RAMAddr), .in_5(D_Data_to_RAM), .RAM_Read(D_RAMread),
    .RAM_Write(D_RAMWrite), .RAM_clock(out_3), .out_13(D_Data_from_RAM), .TTY_Ready(1'b1),
    .out_14(io_1_out_14), .TTY_Clock(io_1_tty_clock), .reset(Reset), .TTY_Clear(io_1_tty_clear),
    .TTY_Enable(io_1_tty_enable));  // open: in_2, KB_Status, KB_Clock, KB_Clear
  Comparator #(.width(4), .mode("unsigned")) comparator_5 (
    .a(icode), .b(4'b1111), .eq(comparator_5_eq));  // open: gt, lt
  Comparator #(.width(4), .mode("unsigned")) comparator_6 (
    .a(icode), .b(4'b1110), .eq(comparator_6_eq));  // open: gt, lt
  TTY tty_1 (.data(io_1_out_14), .clk(io_1_tty_clock), .we(io_1_tty_enable), .clr(io_1_tty_clear));
  or or_2 (or_2_out, priv_bit, comparator_5_eq);
  or or_3 (or_3_out, comparator_6_eq, Reset);
  Register #(.width(1)) register_1 (.D(or_2_out), .Q(priv_bit), .clk(out_3), .clr(or_3_out));  // open: en

  // Other names for the same wires on the sheet: ldPC = FSMOut[0]; newPCsel[1:0] = FSMOut[2:1];
  //   FSMOut (some bits) = {dstEsel, dstEreq, dstMreq, aluAsel, aluBsel, aluOPsel, DMemReq, DMemWrite};
  //   ldMDR = FSMOut[5]; MDRsel = FSMOut[6]; ldMAR = FSMOut[7]; MARsel = FSMOut[8]; ldCC = FSMOut[9];
  //   srcBsel = FSMOut[18]; srcAsel = FSMOut[19]; valCsel = FSMOut[20]; PCIncSel[1:0] = FSMOut[22:21];
  //   IMemReq = FSMOut[23]; Clock = out_3

  // Notes on the sheet:
  //   Fetch
  //   BUG FIX
  //   connect to memory!
  //   valP
  //   FSM ROM
  //   valM
  //   Decode
  //   contents of rom_1 (hex, n*v repeats v):
  //   80000005 3 180d 2 22 26 1012 1015 400001 501 39*0 101 21080101 70980101 7010a109 70108119 20860101
  //   40000701 46b0e309 ea1801d 26b0a109 2ea18119 30840001 70900101 40000301 101
  //   SWS and Taylor Cathcart and Vijay Kothari, based on a skeleton from Matt Kretchmar
  //   rB == F?
  //   Execute
  //   Memory
  //   PC
  //   there is no need to check KBSR -> DDR addresses
  //   because they are above 10000
  //   0x00FFFE00 KBSR
  //   0x00FFFE04 KBDR
  //   0x00FFFE08 DSR
  //   0x00FFFE0C DDR
  //   max ROM addr is 0xffff
  //   living at 0 0x3ff
  //   living at 0x3ff to 0xfffff
  //   contents of rom_2 (hex, n*v repeats v):
  //   61 3 73 27 0 0 0 30 f3 c fe ff 0 30 f0 68 0 0 0 40 3 4*0 f0 30 f0 65 0 0 0 40 3 5*0 30 f0 aa aa 0 0
  //   30 f3 bb bb 0 0 e0
  //   program ROM
  //   Memory mapped IO
  //   icode E for enter_os
  //   no keyboard needed
endmodule

module isplit (
  input  [7:0] B0,
  input  [7:0] B1,
  input  [7:0] B2,
  input  [7:0] B3,
  input  [7:0] B4,
  input  [7:0] B5,
  output [3:0] icode,
  output [3:0] ifun,
  output [3:0] rA,
  output [3:0] rB,
  output [31:0] Dest,
  output [31:0] D_V
);


  assign D_V = {B5, B4, B3, B2};
  assign Dest = {B4, B3, B2, B1};
  assign icode = B0[7:4];
  assign ifun = B0[3:0];
  assign rA = B1[7:4];
  assign rB = B1[3:0];
endmodule

module FSM (
  input  DmemDone,
  input  IMemDone,
  input  Clock,
  output [3:0] icode,
  output [23:0] Output
);

  wire [5:0] current_state_q, microsequencer_1_nextstate;
  wire [7:0] rom_1_data;

  Register #(.width(6)) current_state (
    .D(microsequencer_1_nextstate), .Q(current_state_q), .clk(Clock));  // open: en, clr
  ROM #(.addrWidth(6), .dataWidth(32)) rom_1 (.addr(current_state_q), .data({Output, rom_1_data}));  // open: sel
  microsequencer microsequencer_1 (
    .currentstate(current_state_q), .valN(rom_1_data[7:2]), .DMemDone(DmemDone), .icode(icode),
    .IMemDone(IMemDone), .select(rom_1_data[1:0]), .NextState(microsequencer_1_nextstate));

  // Notes on the sheet:
  //   takes in 6 bit state as addr
  //   spits out 24 bit instruction 
  //   FSM ROM
  //   contents of rom_1 (hex, n*v repeats v):
  //   28000 2c000 30000 34000 38000 3c000 40000 44000 48000 4c000 50000 54000 58000 5c000 60000 68000
  //   d0000 d8000 e0000
endmodule

module test (
  input  [31:0] in_1,
  input  [1:0] icode,
  input  [31:0] in_3,
  input  in_4,
  input  [3:0] in_5,
  output [31:0] out_6
);

  wire [2:0] alu_1_cc;
  wire [31:0] multiplexer_1_out, multiplexer_2_out;

  Multiplexer #(.select(2), .width(32), .enable("false")) multiplexer_1 (
    .in0(in_1), .in1(in_1), .in2(32'h4), .in3(32'hfffffffc), .out(multiplexer_1_out), .sel(icode));
  Multiplexer #(.width(32), .enable("false")) multiplexer_2 (
    .in0(in_3), .in1({32{1'b0}}), .out(multiplexer_2_out), .sel(in_4));
  alu alu_1 (.CC(alu_1_cc), .ALU_A(multiplexer_1_out), .valE(out_6), .ALU_B(multiplexer_2_out), .ALU_op(in_5));
endmodule
